# Fritzing sketch PCB_design (saved by Fritzing 0.9.3b)
circuit board: 9.50095cm x 5.96566cm

parts:
  VCC1 = Battery
  S5 = Pushbutton [package="[SMD]"]
  S4 = Pushbutton [package="[SMD]"]
  S3 = Pushbutton [package="[SMD]"]
  S1 = Pushbutton [package="[SMD]"]
  S2 = Pushbutton [package="[SMD]"]
  S6 = Pushbutton [package="[SMD]"]
  R1 = Resistor [tolerance=±5% resistance=220 package="0603 [SMD]"]
  R2 = Resistor [tolerance=±5% resistance=220 package="0603 [SMD]"]
  R4 = Resistor [tolerance=±5% resistance=220 package="0603 [SMD]"]
  R3 = Resistor [tolerance=±5% resistance=220 package="0603 [SMD]"]
  LED2 = smd LED [color="Red (633nm)" package="0603 [SMD]"]
  LED3 = smd LED [color="Red (633nm)" package="0603 [SMD]"]
  0 = smd LED [color="Red (633nm)" package="0603 [SMD]"]
  LED5 = smd LED [color="Green (565nm)" package="0603 [SMD]"]
  U2 = RJ45 Jack [package=rj45-8]
  U1 = RJ45 Jack [package=rj45-8]
  Part1 = ATTiny4313 [chip_label=IC package=SO(w)]

nets:
  N1: VCC1.-, S5.Pin_3, S5.Pin_4, S4.Pin_3, S4.Pin_4, S3.Pin_1, S3.Pin_2, S1.Pin_3, S2.Pin_3, S6.Pin_3, S6.Pin_4, R1.Pin_0, R4.Pin_1, Part1.10
  N2: S5.Pin_1, S5.Pin_2, Part1.9
  N3: S4.Pin_1, S4.Pin_2, Part1.8
  N4: S3.Pin_3, S3.Pin_4, Part1.7
  N5: S1.Pin_1, S1.Pin_2, Part1.6
  N6: S2.Pin_1, S2.Pin_2, Part1.2
  N7: S6.Pin_1, S6.Pin_2, Part1.11
  N8: R1.Pin_1, LED2.cathode, LED3.cathode, 0.cathode
  N9: R2.Pin_0, U2.3
  N10: R2.Pin_1, Part1.4
  N11: R4.Pin_0, LED5.cathode
  N12: R3.Pin_0, Part1.5
  N13: R3.Pin_1, U1.3
  N14: LED2.anode, Part1.14
  N15: LED3.anode, Part1.15
  N16: 0.anode, Part1.16
  N17: LED5.anode, Part1.13
  N18: U2.1, Part1.3
  N19: U2.2, Part1.1
  N20: U2.5, Part1.17
  N21: U2.7, Part1.18
  N22: U2.8, Part1.19
  N23: U1.1, Part1.12
